// Digital circuit main.dig as structural Verilog
module main (
  input  clk,
  input  reset,
  output [23:0] b,
  output [31:0] a,
  output [31:0] f,
  output [23:0] e,
  output [23:0] i,
  output [7:0] h,
  output [7:0] d,
  output [7:0] g,
  output [7:0] c,
  output [7:0] k,
  output [31:0] j,
  output [31:0] l,
  output [31:0] m,
  output [31:0] p,
  output [15:0] term_data,
  output [15:0] vram_addr,
  output term_we,
  output [31:0] r,
  output [31:0] n,
  output a1,
  output [7:0] a2,
  output [7:0] a3
);

  wire alu_cout, alu_nout, alu_nzout, alu_vout, alu_zout, and_3_out, and_4_out, b_main_sel, comparator_1_eq,
       comparator_2_eq, comparator_3_eq, ctrl_addr_csel, ctrl_branch_en, ctrl_bus_sel, ctrl_cin_sel,
       ctrl_flags_we, ctrl_jump_type, ctrl_mem_rd, ctrl_mem_wr, ctrl_wb_sel, flag_c, flag_n, flag_v, flag_z,
       HALT_IN, is_mmio, mem_rd_out, pc_branch_en, pc_jump_uncond, pc_mux_sel_1, pc_mux_sel_2, ram_cs,
       seq_exec, seq_fetch, sp_load_n, vram_we;
  wire [1:0] ctrl_cycles, ctrl_shift_op, ctrl_sp_op;
  wire [2:0] cond;
  wire [4:0] ctrl_alu_pre;
  wire [15:0] vram_data;
  wire [23:0] CPU_ADDR_OUT, mem_addr, mem_addr_in, mmio_addr, pc_save, sp_delta;
  wire [31:0] alu_b, io_data_in, reg_c, shift_out;

  and and_1 (pc_branch_en, ctrl_branch_en, seq_exec);
  and and_2 (pc_jump_uncond, ctrl_jump_type, seq_exec);
  sequencer sequencer_1 (
    .reset(reset), .cycles(ctrl_cycles), .CLK(clk), .FETCH(seq_fetch), .EXECUTE(seq_exec));  // open: MEM_WAIT
  pc pc_1 (
    .CLK(clk), .nSR(reset), .ADDR_ABS(i), .OFFSET(e), .ADDR_RET(pc_save), .MUX1_SEL(pc_mux_sel_1),
    .MUX2_SEL(pc_mux_sel_2), .FLAG_N(flag_n), .FLAG_C(flag_c), .FLAG_Z(flag_z), .FLAG_O(flag_v), .COND(cond),
    .BRANCH_EN(pc_branch_en), .INT_EN_IN(1'b0), .HALT_IN(HALT_IN), .INT_REQ(1'b0), .INT_VEC_0(1'b1),
    .INT_VEC_1(1'b1), .INT_VEC_2(1'b1), .SP_DELTA(sp_delta), .SP_LOAD_N(sp_load_n),
    .JUMP_UNCOND(pc_jump_uncond), .PCEN(seq_fetch), .PC_OUT(b), .PC_SAVE(pc_save));  // open: INT_EN, HALTED, SP_OUT, INT_ACK, FLAGS_SAVE
  mmio_bus mmio_bus_1 (
    .ADDR(mem_addr), .CPU_ADDR_OUT(CPU_ADDR_OUT), .mmio_addr(mmio_addr), .is_mmio(is_mmio));  // open: cpu_addr_msb2
  Multiplexer #(.Bits(24)) multiplexer_1 (.sel(and_3_out), .in_0(CPU_ADDR_OUT), .in_1(mmio_addr), .out(mem_addr_in));
  and and_3 (and_3_out, is_mmio, mem_rd_out);
  bus_arbitration bus_arbitration_1 (
    .FETCH(seq_fetch), .PC_OUT(b), .IR_ADDR(i), .reg_a(n[23:0]), .MEM_RD_IN(ctrl_mem_rd),
    .addr_sel(ctrl_bus_sel), .ADDR_BUS(mem_addr), .MEM_RD_OUT(mem_rd_out));
  // ir3 ir3_1: pin names not known; wires that end beside it: j, a, seq_fetch, clk, f, c, a2, d, a3, i, e, cond
  EEPROMDualPort #(.AddrBits(24), .Bits(32)) eepromdualport_1 (
    .A(mem_addr), .Din(r), .str(ctrl_mem_wr), .C(clk), .ld(mem_rd_out), .D(a));
  // microcode microcode_1: pin names not known; wires that end beside it: c, k, ctrl_alu_pre, ctrl_cin_sel, ctrl_wb_sel, ctrl_shift_op, ctrl_flags_we, a1, ctrl_mem_rd, ctrl_mem_wr, ctrl_addr_csel, ctrl_branch_en, ctrl_jump_type, ctrl_sp_op, ctrl_cycles
  // register register_1: pin names not known; wires that end beside it: a1, m, a2, d, a3, seq_exec, ctrl_addr_csel, f[23:16], clk, ctrl_bus_sel, b_main_sel, pc_mux_sel_1, n, r, reg_c
  io_controller io_controller_1 (
    .mem_addr(mmio_addr), .c_wr(ctrl_mem_wr), .kb_data(16'h1), .mem_data_out(r), .io_data_in(io_data_in),
    .ram_cs(ram_cs), .vram_we(vram_we), .vram_addr(vram_addr), .vram_data(vram_data), .term_we(term_we),
    .term_data(term_data));
  Comparator #(.Bits(8)) comparator_1 (.a(8'h1), .b(c), .eq(comparator_1_eq));  // open: gt, lt
  Comparator #(.Bits(8)) comparator_2 (.a({8{1'b0}}), .b(a3), .eq(comparator_2_eq));  // open: gt, lt
  Multiplexer #(.Bits(32)) multiplexer_2 (.sel(b_main_sel), .in_0(r), .in_1({{16{1'b0}}, f[23:8]}), .out(alu_b));
  and and_4 (and_4_out, comparator_1_eq, seq_exec, a1, comparator_2_eq);
  shift shift_1 (.A(n), .mode(ctrl_shift_op), .B(r[4:0]), .Out(shift_out));
  alu_32b_final alu_32b_final_1 (
    .A(n), .nz0(1'b0), .B(alu_b), .Opcode(k), .control(ctrl_alu_pre), .REG_C(reg_c), .cin_sel(ctrl_cin_sel),
    .FLAG_C(flag_c), .vout(alu_vout), .zout(alu_zout), .nzout(alu_nzout), .nout(alu_nout), .Out(j),
    .cout(alu_cout));
  flag_reg flag_reg_1 (
    .ZERO_IN(alu_zout), .CARRY_IN(alu_cout), .NEGATIVE_IN(alu_nout), .OVERFLOW_IN(alu_vout),
    .FLAG_WE(ctrl_flags_we), .CLK(clk), .EXEC(seq_exec), .FLAG_Z(flag_z), .FLAG_C(flag_c), .FLAG_N(flag_n),
    .FLAG_O(flag_v));
  // wb_mux wb_mux_1: pin names not known; wires that end beside it: ctrl_wb_sel, j, shift_out, pc_save, a, m
  Register #(.Bits(32)) register_2 (.D(alu_b), .C(clk), .en(and_4_out), .Q(p));
  and and_5 (HALT_IN, comparator_3_eq, seq_exec);
  Comparator #(.Bits(8)) comparator_3 (.a({8{1'b1}}), .b(c), .eq(comparator_3_eq));  // open: gt, lt
  Comparator #(.Bits(8)) comparator_4 (.a(f[31:24]), .b(8'h33), .eq(pc_mux_sel_2));  // open: gt, lt
  Multiplexer #(.Selector_Bits(2), .Bits(24)) multiplexer_3 (
    .sel(ctrl_sp_op), .in_0({24{1'b0}}), .in_1(24'h1), .in_2({24{1'b1}}), .in_3({24{1'b0}}), .out(sp_delta));
  nor nor_1 (sp_load_n, ctrl_sp_op[0], ctrl_sp_op[1]);

  assign g = a2;
  assign h = a3;
  assign l = a;

  // Other names for the same wires on the sheet: alu_out[31:0] = j; ctrl_alu_op[7:0] = k; ctrl_reg_we = a1;
  //   IR_ADDR[23:0] = i; ir_addr_a[7:0] = a2; ir_addr_b[7:0] = d; ir_addr_w[7:0] = a3; ir_bus[31:0] = f;
  //   ir_bus_8_23[15:0] = f[23:8]; ir_bus_8_23_32b[15:0] = f[23:8]; ir_bus_16_23[7:0] = f[23:16];
  //   ir_24_31[7:0] = f[31:24]; ir_offset[23:0] = e; ir_opcode[7:0] = c; mem_din[31:0] = a; pc_out[23:0] = b;
  //   reg_a[31:0] = n; reg_a_24b[23:0] = n[23:0]; reg_b[31:0] = r; reg_b_0_4[4:0] = r[4:0]; reg_w_data[31:0] = m

  // Notes on the sheet:
  //   clk: Hz: 8
  //   reset: default 1
endmodule

/* Test case sub_diag:
clk reset j m n r c g d h
C 1 x x x x x x x x x
C 1 x x x x x x x x x
C 1 x x x x x x x x x
C 1 x x x x x x x x x
C 1 x x x x x x x x x
C 1 x x x x x x x x x
C 1 x x x x x x x x x
C 1 x x x x x x x x x
C 1 x x x x x x x x x
C 1 x x x x x x x x x
C 1 x x x x x x x x x
C 1 x x x x x x x x x
C 1 x x x x x x x x x
C 1 x x x x x x x x x
C 1 x x x x x x x x x
C 1 x x x x x x x x x
C 1 x x x x x x x x x
C 1 x x x x x x x x x
C 1 x x x x x x x x x
C 1 x x x x x x x x x
C 1 x x x x x x x x x
C 1 x x x x x x x x x
C 1 x x x x x x x x x
C 1 x x x x x x x x x
C 1 x x x x x x x x x
C 1 x x x x x x x x x
C 1 x x x x x x x x x
C 1 x x x x x x x x x
C 1 x x x x x x x x x
C 1 x x x x x x x x x
C 1 x x x x x x x x x
C 1 x x x x x x x x x
C 1 x x x x x x x x x
C 1 x x x x x x x x x
C 1 x x x x x x x x x
C 1 x x x x x x x x x
C 1 x x x x x x x x x
C 1 x x x x x x x x x
C 1 x x x x x x x x x
C 1 x x x x x x x x x
C 1 x 7 7 10 3 2 1 2 3
*/
